// Logisim project cpu.circ as structural Verilog: 1 circuit, main circuit main
module main (
  input  CLK_RUN,
  input  [7:0] in_2,
  input  [15:0] in_3,
  input  in_4,
  input  in_5,
  input  HLT,
  input  DATA_TO_IR,
  input  ADDR_TO_IP,
  input  IP_INC,
  input  IP_TO_ADDR,
  input  DATA_TO_A,
  input  A_TO_DATA,
  input  A_TO_X,
  input  ADDR_TO_MAR,
  input  MAR_INC,
  input  SUB,
  input  Z_TO_DATA,
  input  MDR_TO_DATA,
  input  DATA_TO_MDR,
  input  FLAGS,
  input  ADDR_TO_HL,
  input  HL_TO_ADDR,
  input  DATA_TO_Y,
  input  ADDR_TO_HL_2,
  input  DATA_TO_B,
  input  T_TO_ADDR,
  input  B_TO_DATA,
  input  DATA_TO_C,
  input  C_TO_DATA,
  input  ADDR_TO_SP,
  input  SP_DEC,
  input  SP_TO_ADDR,
  input  SP_INC,
  input  DATA_TO_D,
  input  D_TO_DATA,
  input  DATA_TO_ADDR_HI,
  input  ADDR_HI_TO_DATA,
  input  DATA_TO_ADDR_LO,
  input  ADDR_LO_TO_DATA,
  output [3:0] out_40,
  output [7:0] out_41,
  output [15:0] out_42,
  output [15:0] out_43,
  output [7:0] out_44,
  output [7:0] out_45,
  output [15:0] out_46,
  output [7:0] out_47,
  output [7:0] out_48,
  output [7:0] out_49,
  output [7:0] out_50,
  output [7:0] out_51,
  output [15:0] out_52,
  output [7:0] _C_Z,
  output [15:0] out_54,
  output [7:0] out_55,
  output [7:0] out_56,
  output [15:0] out_57,
  output [7:0] out_58,
  output [7:0] out_59
);

  wire adder_1_cout, and_1_out, and_2_out, and_4_out, and_5_out, and_6_out, and_7_out, and_8_out, and_9_out,
       and_10_out, and_11_out, CLK, CLK_STEP_out, clock_1_out, minus_CLK, nor_1_out, not_1_out, not_2_out,
       not_4_out, or_1_out, or_2_out, or_3_out, or_4_out, or_5_out, or_6_out, or_7_out, or_8_out, or_9_out,
       or_10_out, or_11_out, RST;
  wire [7:0] bit_extender_1_out, xor_1_out;

  Button CLK_STEP (.out(CLK_STEP_out));
  Button u_RST (.out(RST));
  Clock clock_1 (.out(clock_1_out));
  and and_1 (and_1_out, clock_1_out, CLK_RUN);
  not not_1 (not_1_out, CLK_RUN);
  and and_2 (and_2_out, not_1_out, CLK_STEP_out);
  or or_1 (or_1_out, and_1_out, and_2_out);
  and and_3 (CLK, or_1_out, not_2_out);
  not not_2 (not_2_out, HLT);
  Register register_1 (.D(out_41), .en(DATA_TO_IR), .Q(out_44), .clk(CLK), .clr(RST));
  Register register_2 (.D(out_41), .en(DATA_TO_A), .Q(out_45), .clk(CLK));  // open: clr
  Register register_3 (.D(out_45), .en(A_TO_X), .Q(out_47), .clk(CLK));  // open: clr
  assign bit_extender_1_out = {{7{SUB}}, SUB};  // Bit_Extender bit_extender_1
  Register register_4 (.D(out_41), .en(DATA_TO_Y), .Q(out_55), .clk(CLK));  // open: clr
  Register register_5 (.D(out_41), .en(DATA_TO_B), .Q(out_56), .clk(CLK));  // open: clr
  Register register_6 (.D(out_41), .en(DATA_TO_C), .Q(out_58), .clk(CLK));  // open: clr
  Register register_7 (.D(out_41), .en(DATA_TO_D), .Q(out_59), .clk(CLK));  // open: clr
  Counter #(.width(4), .max('hf)) counter_1 (.count(1'b1), .Q(out_40), .clk(minus_CLK));  // open: load, D, carry, clr
  not not_3 (minus_CLK, CLK);
  assign out_41 = A_TO_DATA ? out_45 : 8'bz;  // Controlled_Buffer controlled_buffer_1
  Adder adder_1 (.a(out_47), .b(xor_1_out), .out(out_48), .cin(SUB), .cout(adder_1_cout));
  assign xor_1_out = bit_extender_1_out ^ out_55;  // XOR_Gate xor_1, 8 bits wide
  nor nor_1 (nor_1_out, out_48[0], out_48[1], out_48[2], out_48[3], out_48[4], out_48[5], out_48[6], out_48[7]);
  assign out_41 = B_TO_DATA ? out_56 : 8'bz;  // Controlled_Buffer controlled_buffer_2
  assign out_41 = C_TO_DATA ? out_58 : 8'bz;  // Controlled_Buffer controlled_buffer_3
  assign out_41 = D_TO_DATA ? out_59 : 8'bz;  // Controlled_Buffer controlled_buffer_4
  assign out_41 = Z_TO_DATA ? out_48 : 8'bz;  // Controlled_Buffer controlled_buffer_5
  D_Flip_Flop d_ff_1 (.clk(CLK), .D(nor_1_out), .Q(_C_Z[0]), .en(FLAGS), .reset(RST));  // open: Qn, preset
  D_Flip_Flop d_ff_2 (.clk(CLK), .D(adder_1_cout), .Q(_C_Z[1]), .en(FLAGS), .reset(RST));  // open: Qn, preset
  assign out_41 = in_4 ? in_2 : 8'bz;  // Controlled_Buffer controlled_buffer_6
  assign out_49 = DATA_TO_MDR ? out_41 : 8'bz;  // Controlled_Buffer controlled_buffer_7
  assign out_41 = MDR_TO_DATA ? out_49 : 8'bz;  // Controlled_Buffer controlled_buffer_8
  assign out_42[7:0] = DATA_TO_ADDR_LO ? out_41 : 8'bz;  // Controlled_Buffer controlled_buffer_9
  assign out_42[15:8] = DATA_TO_ADDR_HI ? out_41 : 8'bz;  // Controlled_Buffer controlled_buffer_10
  not not_4 (not_4_out, DATA_TO_MDR);
  or or_2 (or_2_out, ADDR_TO_SP, SP_DEC);
  or or_3 (or_3_out, SP_DEC, SP_INC);
  Counter #(.width(16), .max('hffff)) counter_2 (
    .load(ADDR_TO_IP), .D(out_42), .count(IP_INC), .Q(out_43), .clk(CLK), .clr(RST));  // open: carry
  Counter #(.width(16), .max('hffff)) counter_3 (
    .load(ADDR_TO_MAR), .D(out_42), .count(MAR_INC), .Q(out_46), .clk(CLK));  // open: carry, clr
  Register #(.width(16)) register_8 (.D(out_42), .en(ADDR_TO_HL), .Q({out_51, out_50}), .clk(CLK));  // open: clr
  Register #(.width(16)) register_9 (.D(out_42), .en(ADDR_TO_HL_2), .Q(out_54), .clk(CLK));  // open: clr
  Counter #(.width(16), .max('hffff)) counter_4 (
    .load(or_2_out), .D(out_42), .count(or_3_out), .Q(out_57), .clk(CLK), .clr(RST));  // open: carry
  RAM #(.addrWidth(16)) ram_1 (.addr(out_46), .data(out_49), .sel(1'b1), .clk(CLK), .ld(not_4_out));  // open: clr
  assign out_42[7:0] = or_4_out ? out_43[7:0] : 8'bz;  // Controlled_Buffer controlled_buffer_11
  and and_4 (and_4_out, ADDR_TO_IP, DATA_TO_ADDR_HI);
  or or_4 (or_4_out, and_4_out, IP_TO_ADDR);
  and and_5 (and_5_out, ADDR_TO_IP, DATA_TO_ADDR_LO);
  or or_5 (or_5_out, IP_TO_ADDR, and_5_out);
  assign out_42[7:0] = or_6_out ? out_50 : 8'bz;  // Controlled_Buffer controlled_buffer_12
  and and_6 (and_6_out, ADDR_TO_HL, DATA_TO_ADDR_HI);
  or or_6 (or_6_out, and_6_out, HL_TO_ADDR);
  or or_7 (or_7_out, HL_TO_ADDR, and_7_out);
  and and_7 (and_7_out, ADDR_TO_HL, DATA_TO_ADDR_LO);
  assign out_42[7:0] = or_8_out ? out_54[7:0] : 8'bz;  // Controlled_Buffer controlled_buffer_13
  and and_8 (and_8_out, ADDR_TO_HL_2, DATA_TO_ADDR_HI);
  or or_8 (or_8_out, and_8_out, T_TO_ADDR);
  and and_9 (and_9_out, ADDR_TO_HL_2, DATA_TO_ADDR_LO);
  or or_9 (or_9_out, T_TO_ADDR, and_9_out);
  assign out_42[7:0] = or_10_out ? out_57[7:0] : 8'bz;  // Controlled_Buffer controlled_buffer_14
  and and_10 (and_10_out, ADDR_TO_SP, DATA_TO_ADDR_HI);
  or or_10 (or_10_out, and_10_out, SP_TO_ADDR);
  or or_11 (or_11_out, SP_TO_ADDR, and_11_out);
  and and_11 (and_11_out, ADDR_TO_SP, DATA_TO_ADDR_LO);
  assign out_41 = ADDR_HI_TO_DATA ? out_42[15:8] : 8'bz;  // Controlled_Buffer controlled_buffer_15
  assign out_42 = in_5 ? in_3 : 16'bz;  // Controlled_Buffer controlled_buffer_16
  assign out_42[15:8] = or_5_out ? out_43[15:8] : 8'bz;  // Controlled_Buffer controlled_buffer_17
  assign out_42[15:8] = or_7_out ? out_51 : 8'bz;  // Controlled_Buffer controlled_buffer_18
  assign out_42[15:8] = or_9_out ? out_54[15:8] : 8'bz;  // Controlled_Buffer controlled_buffer_19
  assign out_42[15:8] = or_11_out ? out_57[15:8] : 8'bz;  // Controlled_Buffer controlled_buffer_20
  assign out_41 = ADDR_LO_TO_DATA ? out_42[7:0] : 8'bz;  // Controlled_Buffer controlled_buffer_21

  assign _C_Z[7:2] = {6{1'b0}};
  assign out_52 = {out_51, out_50};

  // Other names for the same wires on the sheet: ZF = _C_Z[0]; CF = _C_Z[1]

  // Notes on the sheet:
  //   Microsequencer
  //   Clock
  //   A Register
  //   X Register
  //   Y Register
  //   B Register
  //   C Register
  //   D Register
  //   Instruction Register
  //   Adder / Subtractor
  //   Flags
  //   8-Bit Data Bus
  //   Z Register
  //   Memory Address Register
  //   L Register
  //   H Register
  //   Instruction Pointer
  //   Memory Data Register
  //   HL Register
  //   T Register
  //   Stack Pointer
  //   16-Bit Address Bus
endmodule
